# Fritzing sketch PCB-CENG 318 (saved by Fritzing 0.9.3b)
circuit board: 8.46667cm x 5.64444cm
breadboards: 1

parts:
  M1 = STM32F103C8T6 blue mini board
  LED1 = RGB LED (com. cathode, rbg) [package="5 mm [THT]"]
  R1 = Resistor [tolerance=±5% resistance=220 package="1206 [SMD]"]
  R2 = Resistor [tolerance=±5% resistance=220 package="1206 [SMD]"]
  R3 = Resistor [tolerance=±5% resistance=220 package="1206 [SMD]"]

nets (from the pcb view):
  N1: M1.B7, R3.Pin_0
  N2: M1.B8, LED1.blue_anode, LED1.green_anode, R2.Pin_0, R2.Pin_1, R3.Pin_1
  N3: M1.5V, LED1.red_anode, R1.Pin_1
  N4: M1.G, M1.GND, LED1.common_cathode
